# Fritzing sketch final (saved by Fritzing 0.9.3b)
breadboards: 1

parts:
  元件1 = Arduino Uno (Rev3)
  M1 = DC Motor
  M2 = DC Motor
  hc-sr1 = hc-sr04
  hc-sr2 = hc-sr04
  VCC2 = Battery  # not connected
  L298N1 = L298N DC motor driver
  R1 = Resistor [tolerance=±5% resistance=220 package=THT]
  M3 = fc-51 [package=THT]
  M4 = fc-51 [package=THT]
  M5 = fc-51 [package=THT]
  M6 = fc-51 [package=THT]

nets:
  N1: 元件1.A2, M6.pin1
  N2: 元件1.A3, M5.pin1
  N3: 元件1.A4/SDA, M4.pin1
  N4: 元件1.A5/SCL, M3.pin1
  N5: 元件1.D8, hc-sr1.Trig
  N6: 元件1.D9_PWM, L298N1.IN2
  N7: 元件1.D10_PWM/SS, L298N1.IN1
  N8: 元件1.D11_PWM/MOSI, L298N1.ENA
  N9: 元件1.D2, hc-sr2.Trig
  N10: 元件1.D3_PWM, hc-sr2.Echo
  N11: 元件1.D4, L298N1.IN4
  N12: 元件1.D5_PWM, L298N1.IN3
  N13: 元件1.D6_PWM, L298N1.ENB
  N14: 元件1.D7, hc-sr1.Echo
  VCC: 元件1.5V, hc-sr1.VCC, hc-sr2.VCC, R1.Pin_0, R1.Pin_1, M3.pin3, M4.pin3, M5.pin3, M6.pin3
  GND: 元件1.GND, hc-sr1.GND, hc-sr2.GND, L298N1.GND, M3.pin2, M4.pin2, M5.pin2, M6.pin2
  VIN: 元件1.VIN, L298N1.5V
  N15: M1.pin_1, L298N1.OUT4
  N16: M1.pin_2, L298N1.OUT3
  N17: M2.pin_1, L298N1.OUT2
  N18: M2.pin_2, L298N1.OUT1

custom parts:
  Battery: Your standard 2x 18650 battery pack (7,4 Volts)
  L298N DC motor driver: 2x DC motor driver with 78M05 positive voltage regulator (7..35 V) L298N: max 46 V, 2 A Set 5 V Enable jumper to enable 5 V regultor (needed for the L298N) and +5 V output at screw terminal or supply external +5 V at screw terminal Set ENA and/or ENB to +5 V to enable motor permanently or supply ENA and/or ENB with PWM signal IN1 and IN2 set rotation directory for motor A (OUT1/OUT2) IN2 and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
