# Fritzing sketch Lab7-2 (saved by Fritzing 0.9.3b)

parts:
  DHT11_1 = DHT11 module
  元件1 = Arduino Uno (Rev3)

nets:
  VCC: DHT11_1.VCC, 元件1.5V
  GND: DHT11_1.GND, 元件1.GND
  N1: DHT11_1.DATA, 元件1.D6_PWM

custom parts:
  DHT11 module: DHT11 black pcb module
