# Fritzing sketch layout (saved by Fritzing 0.9.3b)
breadboards: 1

parts:
  元件1 = Arduino Uno (Rev3)
  hc-sr1 = hc-sr04

nets:
  N1: 元件1.D11_PWM/MOSI, hc-sr1.Echo
  N2: 元件1.D12/MISO, hc-sr1.Trig
  5V: 元件1.5V, hc-sr1.VCC
  GND: 元件1.GND, hc-sr1.GND
