# Fritzing sketch Lab8-2 (saved by Fritzing 0.9.3b)
breadboards: 1

parts:
  LCD1 = LCD screen
  元件1 = Arduino Uno (Rev3)
  LCM1602_IIC1 = LCM1602 IIC [part_number="LCM1602 IIC" chip_label="LCM1602 IIC" package="DIP (Dual Inline) [THT]"]
  DHT11_1 = DHT11 module
  hc-sr1 = hc-sr04

nets:
  VSS: LCD1.VSS, LCM1602_IIC1.VSS
  VDD: LCD1.VDD, LCM1602_IIC1.VDD
  N1: LCD1.V0, LCM1602_IIC1.V0
  N2: LCD1.RS, LCM1602_IIC1.RS
  N3: LCD1.R/W, LCM1602_IIC1.RW
  N4: LCD1.E, LCM1602_IIC1.E
  N5: LCD1.DB0, LCM1602_IIC1.D0
  N6: LCD1.DB1, LCM1602_IIC1.D1
  N7: LCD1.DB2, LCM1602_IIC1.D2
  N8: LCD1.DB3, LCM1602_IIC1.D3
  N9: LCD1.DB4, LCM1602_IIC1.D4
  N10: LCD1.DB5, LCM1602_IIC1.D5
  N11: LCD1.DB6, LCM1602_IIC1.D6
  N12: LCD1.DB7, LCM1602_IIC1.D7
  N13: LCD1.LED+, LCM1602_IIC1.A
  N14: LCD1.LED-, LCM1602_IIC1.K
  N15: 元件1.A4/SDA, LCM1602_IIC1.SDA
  N16: 元件1.A5/SCL, LCM1602_IIC1.SCL
  N17: 元件1.D11_PWM/MOSI, hc-sr1.Echo
  N18: 元件1.D12/MISO, hc-sr1.Trig
  N19: 元件1.D5_PWM, DHT11_1.DATA
  VCC: 元件1.5V, LCM1602_IIC1.VCC, DHT11_1.VCC, hc-sr1.VCC
  GND: 元件1.GND, LCM1602_IIC1.GND, DHT11_1.GND, hc-sr1.GND

custom parts:
  LCM1602 IIC: I2C-Module to use a 1602 or 2004 LCD on with the wire.h libory Serial LCD Modul
  DHT11 module: DHT11 black pcb module
